# Fritzing sketch Xia_Jefferson_Fritzing_Diagram (saved by Fritzing 0.9.8b)
breadboards: 1

parts:
  Part1 = PocketBeagle
  SM1 = 28BYJ-48 Stepper Motor [part_number=28BYJ-48]  # not connected
  SM2 = 28BYJ-48 Stepper Motor [part_number=28BYJ-48]  # not connected
  Driver1 = 28BYJ-48 Driver Module [part_number=ULN2003 package=THT]
  Driver2 = 28BYJ-48 Driver Module [part_number=ULN2003 package=THT]

nets:
  GND: Part1.GND, Driver1.GND, Driver2.GND
  N1: Part1.VOUT, Driver1.Vmotor, Driver2.Vmotor

custom parts:
  28BYJ-48 Stepper Motor: Unipolar Stepper Motor 28BYJ-48 Top coil - pink & orange Bottom coil - blue & yellow Common rail - red Connector pins: blue - pink - yellow - orange - red
  28BYJ-48 Driver Module: ULN2003 Driver Module for the 28BYJ-48 Unipolar Stepper Motor LED A - Blue wire - Bottom coil left LED B - Pink wire - Top coil left LED C - Yellow wire - Bottom coil right LED D - Orange wire - Top coil right Common rail - red Connector pins: blue - pink - yellow - orange - red Control pins - IN1 to IN4 Power pins - GND & Vmotor (5-12V) On/Off jumper (if removed, power to motor is cut).
